# Fritzing sketch wiring (saved by Fritzing 0.9.2b)
perfboards: 1

parts:
  WeMos_D1_Mini1 = WeMos D1 Mini
  Part2 = NCP1400 Step-Up Breakout
  Part1 = TP4056 Charger 6pin
  Part3 = Si7021 Temperature and Humidity Sensor [package=Si7021]
  Part4 = Lithium Ion Cylindrical Battery 3.7v 2200mAh [part_number=1781]
  Part5 = Solar Cell
  C1 = Electrolytic Capacitor [capacitance=1µF package="100 mil [THT, electrolytic]"]
  R1 = Resistor [tolerance=±5% resistance=100k package=THT]

nets:
  3V3: WeMos_D1_Mini1.3V3, Part3.VIN
  5V: WeMos_D1_Mini1.5V, Part2.5V, C1.+
  N1: WeMos_D1_Mini1.A0, R1.Pin_0
  N2: WeMos_D1_Mini1.D1, Part3.SDA
  N3: WeMos_D1_Mini1.D2, Part3.SCL
  GND: WeMos_D1_Mini1.G, Part2.GND, Part3.GND, C1.-
  N4: Part2.IN+, Part1.OUT+
  N5: Part2.IN-, Part1.OUT-
  N6: Part1.IN+, Part1.BAT+, Part4.positive, Part5.-
  N7: Part1.IN-, Part1.BAT-, Part4.negative, Part5.+

custom parts:
  WeMos D1 Mini: The D1 mini is a mini wifi board based on ESP-8266EX.
  NCP1400 Step-Up Breakout: Description: The NCP1400 is a 3.3V DC-DC converter. The breakout board will accept voltage inputs between 1 and 3 Volts (such as 1 or 2 AA batteries) and output a constant, low ripple 3.3V output capable of sourcing up to 100 mA. This board is great for supplying power to 3.3V sensors or providing 3.3V from a a single AA battery. The breakout board includes the necessary peripheral components.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
  Lithium Ion Cylindrical Battery 3.7v 2200mAh: This lithium ion battery has a capacity of 2200mAh and a protection circuit that provides over-voltage, under-voltage and over-current protection. This cell can provide 2C of peak current (4400mA). Note that these batteries are not designed to sustain such high loads, we suggest keeping any constant current draw under about 0.5C (1 Amp).
